# Fritzing sketch Untitled Sketch 2 (saved by Fritzing 0.8.7b)

parts:
  Raspberry_Pi_1 = Raspberry Pi 3 [part_number=RPI-3-V1.2]
  IC1 = Rasberry Pi NIOR Camera [chip_label=IC package="DIP (Dual Inline) [THT]"]  # not connected
  Mod1 = gy-906

nets:
  N1: Raspberry_Pi_1.GPIO2, Mod1.GND
  N2: Raspberry_Pi_1.GND, Mod1.SCL
  5V: Raspberry_Pi_1.5V, Mod1.VIN

notes:
  5v power supply

custom parts:
  Rasberry Pi NIOR Camera: Camera
  gy-906: gy-906 Non-contact PIR I2C interface temperature sensor breakout board.
